# Fritzing sketch K130enc2 (saved by Fritzing 0.9.3b)
circuit board: 12.0038cm x 3.99622cm
breadboards: 1

parts:
  J3 = female pin header, 12 pins [form="♀ (female)"]
  J4 = female pin header, 11 pins [form="♀ (female)"]
  CONN1 = USB connector [package=THT]
  IC2 = IC, DIP package, 12 pins [chip_label=IC]
  J17 = female pin header, 5 pins [form="♀ (female)"]
  J18 = female pin header, 5 pins [form="♀ (female)"]
  U1 = USB Connectors [package=usb-microb]
  Pad1 = Pad [width=1.8 height=1.8 connect=center]
  Pad2 = Pad [width=1.8 height=1.8 connect=center]
  J15 = female pin header, 14 pins [form="♀ (female)"]
  J14 = female pin header, 14 pins [form="♀ (female)"]
  J19 = female pin header, 1 pin [form="♀ (female)"]
  J22 = female pin header, 5 pins [form="♀ (female)"]
  J21 = female pin header, 5 pins [form="♀ (female)"]
  J20 = female pin header, 5 pins [form="♀ (female)"]
  R1 = Resistor [tolerance=±5% resistance=220 package=THT]
  R2 = Resistor [tolerance=±5% resistance=220 package=THT]
  R3 = Resistor [tolerance=±5% resistance=220 package=THT]
  J23 = female pin header, 4 pins [form="♀ (female)"]
  J24 = female pin header, 4 pins [form="♀ (female)"]
  J25 = female pin header, 4 pins [form="♀ (female)"]

nets:
  N1: J3.pin1, J14.pin4
  N2: J3.pin2, J14.pin5
  N3: J3.pin3, J14.pin6
  N4: J3.pin4, J14.pin7
  N5: J3.pin5, J14.pin8
  N6: J3.pin6, J14.pin9
  N7: J3.pin7, J14.pin10
  N8: J3.pin8, J14.pin11
  N9: J3.pin9, J14.pin12
  N10: J3.pin10, J14.pin13
  N11: J3.pin11, J18.pin5
  N12: J3.pin12, J17.pin5
  N13: J4.pin1, J15.pin4
  N14: J4.pin2, J15.pin5
  N15: J4.pin3, J15.pin6
  N16: J4.pin4, J15.pin7
  N17: J4.pin5, J15.pin8
  N18: J4.pin6, J15.pin9
  N19: J4.pin7, J15.pin10
  N20: J4.pin8, J15.pin11
  N21: J4.pin9, J15.pin12
  N22: J4.pin10, J15.pin13
  N23: J4.pin11, J15.pin14
  N24: CONN1.5V, U1.VBUS, J19.pin1, J23.pin4, J25.pin4
  N25: CONN1.d-, U1.D-, J23.pin3, J25.pin3
  N26: CONN1.d+, U1.D+, J23.pin2, J25.pin2
  GND: CONN1.GND, CONN1.chassis5, CONN1.chassis6, IC2.pin7, IC2.pin8, IC2.pin9, IC2.pin10, IC2.pin11, IC2.pin12, U1.GND, Pad1.pad, Pad2.pad, J15.pin1, J14.pin2, J22.pin4, J21.pin4, J20.pin4, R1.Pin_1, R2.Pin_1, R3.Pin_1, J23.pin1, J24.pin1, J25.pin1
  N27: IC2.pin1, J17.pin2
  N28: IC2.pin2, J18.pin2
  N29: IC2.pin3, J17.pin3
  N30: IC2.pin4, J18.pin3
  N31: IC2.pin5, J17.pin4
  N32: IC2.pin6, J18.pin4
  N33: J17.pin1, J22.pin2
  N34: J18.pin1, J22.pin5, J21.pin2
  N35: J15.pin2, J24.pin2
  N36: J15.pin3, J24.pin3
  N37: J14.pin1, J22.pin3, J21.pin3, J20.pin3, J24.pin4
  N38: J14.pin14, J21.pin5, J20.pin2
  N39: J22.pin1, R3.Pin_0
  N40: J21.pin1, R2.Pin_0
  N41: J20.pin1, R1.Pin_0

notes:
  VUSB
  25
  27
  29
  31
  33
  24
  26
  28
  30
  32
  GD
  RX
  TX
  2
  3
  4
  5
  6
  7
  8
  9
  10
  11
  12
  VI
  3V
  23
  22
  20
  18
  16
  14
  21
  19
  17
  15
  13
  K130
  github.com/RebeccaRGB/K130
  encoder
  LED3
  LED2
  LED1
  OUT
  GND
  5V
  IN/+
  LED-
  VIN
  D-
  D+
  RevB
  J3
  J4
