# Fritzing sketch ledstrip (saved by Fritzing 0.9.3b)
circuit board: 8cm x 0.8cm
breadboards: 1

parts:
  LED1 = RGB LED - (4 legs) [package="5 mm [THT]"]
  LED2 = RGB LED - (4 legs) [package="5 mm [THT]"]
  LED3 = RGB LED - (4 legs) [package="5 mm [THT]"]
  LED4 = RGB LED - (4 legs) [package="5 mm [THT]"]
  LED5 = RGB LED - (4 legs) [package="5 mm [THT]"]
  LED6 = RGB LED - (4 legs) [package="5 mm [THT]"]
  LED7 = RGB LED - (4 legs) [package="5 mm [THT]"]
  LED8 = RGB LED - (4 legs) [package="5 mm [THT]"]
  J1 = female pin header, 3 pins [form="♀ (female)"]
  J2 = female pin header, 3 pins [form="♀ (female)"]
  Pad1 = Pad [width=1.5 height=1.5 connect=center]
  Pad2 = Pad [width=1.5 height=1.5 connect=center]
  Pad3 = Pad [width=1.5 height=1.5 connect=center]
  Pad4 = Pad [width=1.5 height=1.5 connect=center]

nets:
  N1: LED1.red_cathode, LED2.blue_cathode
  N2: LED1.common_anode, LED2.common_anode, LED3.common_anode, LED4.common_anode, LED5.common_anode, LED6.common_anode, LED7.common_anode, LED8.common_anode, J1.pin3, J2.pin3
  N3: LED1.green_cathode, LED2.green_cathode, LED3.green_cathode, LED4.green_cathode, LED5.green_cathode, LED6.green_cathode, LED7.green_cathode, LED8.green_cathode, J1.pin1, J2.pin1
  N4: LED1.blue_cathode, J1.pin2, Pad1.pad, Pad3.pad
  N5: LED2.red_cathode, LED3.blue_cathode
  N6: LED3.red_cathode, LED4.blue_cathode
  N7: LED4.red_cathode, LED5.blue_cathode
  N8: LED5.red_cathode, LED6.blue_cathode
  N9: LED6.red_cathode, LED7.blue_cathode
  N10: LED7.red_cathode, LED8.blue_cathode
  N11: LED8.red_cathode, J2.pin2, Pad2.pad, Pad4.pad

notes:
  +
  >
  -
  DIN
  DOUT
